# Fritzing sketch Scan-y connection diagram (saved by Fritzing 0.9.3b)
breadboards: 1

parts:
  Raspberry_Pi_1 = Raspberry Pi 3 [part_number=RPI-3-V1.2]
  Pololu_A1 = Pololu A4988 [package=SO16]
  M1 = Stepper Motor - Bipolar
  C2 = Electrolytic Capacitor [capacitance=100µF package="200 mil [THT, electrolytic]"]
  Pi_Camera_V2 = TRANSCHIPTC5747 [package=camera_sfv24r-2st_2]  # not connected

nets:
  N1: Raspberry_Pi_1.GPIO21, Pololu_A1.DIR
  N2: Raspberry_Pi_1.GPIO20, Pololu_A1.STEP
  N3: Raspberry_Pi_1.GPIO7, Pololu_A1.MS3
  N4: Raspberry_Pi_1.GPIO8, Pololu_A1.MS2
  N5: Raspberry_Pi_1.GPIO25, Pololu_A1.MS1
  N6: Raspberry_Pi_1.GND, Pololu_A1.GND#8
  5V: Raspberry_Pi_1.5V, Pololu_A1.VDD
  N7: Pololu_A1.RESET, Pololu_A1.SLEEP
  N8: Pololu_A1.1B, M1.D
  N9: Pololu_A1.1A, M1.B
  N10: Pololu_A1.2A, M1.C
  N11: Pololu_A1.2B, M1.A
  N12: Pololu_A1.GND#14, C2.-
  N13: Pololu_A1.VMOT, C2.+

notes:
  motor power supply 12V
  Micro USB power input 2.5A
  HDMI проектор Excelvan T260
  microSD SanDisk Extreme 32GB
